# Fritzing sketch Infinity Band1 (saved by Fritzing 0.9.1b)
circuit board: 6.01126cm x 6.0777cm
breadboards: 1

parts:
  Part1 = LightBlue Bean
  neopixel1 = Neopixel Ring 12
  S1 = Pushbutton [package="[SMD]"]
  Part2 = Power Cell LiPo Charger/Booster
  U1 = LIPO-110mAh [package=lipo-110]  # not connected

nets:
  VCC: Part1.VCC, neopixel1.VCC
  N1: Part1.D5/SCK, neopixel1.IN
  N2: Part1.D0, S1.Pin_1, S1.Pin_2
  GND: Part1.GND, neopixel1.GND, S1.Pin_3, S1.Pin_4, Part2.GND
  N3: Part1.BAT, Part2.VCC

custom parts:
  Neopixel Ring 12: Neopixel Ring x12
